// Logisim project 16-bit Computer.circ as structural Verilog: 6 circuits, main circuit main
module main (
  input  Signed,
  input  [15:0] Bus_Override,
  input  in_3,
  input  [3:0] Op_Sel,
  input  Power,
  input  Manual_Override,
  input  in_7,
  input  in_8,
  input  in_9,
  input  in_10,
  input  in_11,
  input  in_12,
  input  in_13,
  input  in_14,
  input  in_15,
  input  in_16,
  input  in_17,
  output [3:0] out_18,
  output [15:0] out_19
);

  wire A_In, ALU_Out, AX_In, AX_Out, B_In, bin2dec_1_negative, BP_In, BP_Out, button_1_out, button_2_out,
       button_3_out, button_4_out, button_5_out, button_6_out, button_7_out, button_8_out, button_9_out,
       button_10_out, button_11_out, button_12_out, button_13_out, BX_In, BX_Out, clock_1_out,
       comparator_1_eq, comparator_1_gt, comparator_1_lt, comparator_2_gt, comparator_2_lt, CX_In, CX_Out,
       decoder_1_out1, decoder_1_out2, decoder_1_out3, decoder_1_out4, decoder_1_out5, decoder_1_out6,
       decoder_1_out7, decoder_1_out8, decoder_1_out9, decoder_1_out10, DX_In, DX_Out, Halt, I_In, JA_out,
       JB_out, JE_out, JG_out, JL_out, JNA_out, JNB_out, JNE_out, JNG_out, JNL_out, Manual_Tick_out, MAR_In,
       not_1_out, not_2_out, not_3_out, not_4_out, not_5_out, not_6_out, or_23_out, PC_Inc, PC_Out, PC_Set,
       RAM_In, RAM_Out, Reset_Counter, SP_In, SP_Out;
  wire [3:0] bin2dec_1_bcd_output, bin2dec_1_bcd_output_2, bin2dec_1_bcd_output_3, bin2dec_1_bcd_output_4,
       bin2dec_1_bcd_output_5, I_q, I_q_2, I_q_3, I_q_4, or_1_out, or_7_out_2, rom_1_data, rom_1_data_2,
       rom_2_data_2;
  wire [4:0] counter_1_q;
  wire [15:0] A_q, alu_1_alu_out, and_1_out, and_2_out, and_3_out, and_4_out, and_5_out, and_6_out,
       and_7_out, and_8_out, and_9_out, and_10_out, AX_q, B_q, BP_q, BX_q, CX_q, DX_q, MAR_q, or_7_out,
       or_8_out, or_29_out, ram_1_data, SP_q;
  wire [19:0] rom_2_data;
  wire [31:28] rom_2_data_3;

  Hex_Digit_Display hex_digit_display_1 (.value(or_7_out[15:12]));  // open: dp
  Hex_Digit_Display hex_digit_display_2 (.value(or_7_out_2));  // open: dp
  Hex_Digit_Display hex_digit_display_3 (.value(or_7_out[11:8]));  // open: dp
  Button Manual_Tick (.out(Manual_Tick_out));
  _7_Segment_Display u_7_segment_display_1 (.g(bin2dec_1_negative));  // open: f, a, b, e, d, c, dp
  Hex_Digit_Display hex_digit_display_4 (.value(or_7_out[3:0]));  // open: dp
  assign and_1_out = Bus_Override & {16{in_3}};  // AND_Gate and_1, 16 bits wide
  assign or_1_out = Op_Sel | out_18;  // OR_Gate or_1, 4 bits wide
  Clock clock_1 (
    .Power(Power), .Manual_Override(Manual_Override), .Manual_Tick(Manual_Tick_out), .Halt(Halt),
    .Out(clock_1_out));
  or or_2 (AX_Out, rom_2_data[15], in_7);
  or or_3 (BX_Out, rom_2_data[16], in_11);
  or or_4 (CX_Out, rom_2_data[17], in_12);
  or or_5 (DX_Out, rom_2_data[18], in_14);
  or or_6 (Halt, rom_2_data[19], in_15);
  Hex_Digit_Display hex_digit_display_5 (.value(bin2dec_1_bcd_output_4));  // open: dp
  Hex_Digit_Display hex_digit_display_6 (.value(bin2dec_1_bcd_output_5));  // open: dp
  ALU alu_1 (.Operation(or_1_out), .A(A_q), .B(B_q), .ALU_Out(alu_1_alu_out));
  Register #(.width(16), .trigger("falling")) A (
    .D({or_7_out[15:8], or_7_out_2, or_7_out[3:0]}), .Q(A_q), .clk(A_In));  // open: en, clr
  Register #(.width(16), .trigger("falling")) B (
    .D({or_7_out[15:8], or_7_out_2, or_7_out[3:0]}), .Q(B_q), .clk(B_In));  // open: en, clr
  Register #(.width(16), .trigger("falling")) I (
    .D({or_7_out[15:8], or_7_out_2, or_7_out[3:0]}), .Q({I_q_4, I_q_3, I_q_2, I_q}), .clk(I_In));  // open: en, clr
  Counter #(.width(5), .max('h12)) counter_1 (
    .Q(counter_1_q), .clk(clock_1_out), .clr(Reset_Counter));  // open: load, D, count, carry
  ROM #(.addrWidth(5)) rom_1 (.addr(counter_1_q), .data({rom_1_data, rom_1_data_2}));  // open: sel
  ROM #(.addrWidth(20), .dataWidth(32)) rom_2 (
    .addr({I_q_4, I_q_3, I_q_2, I_q, rom_1_data}), .data({rom_2_data_3, out_18, rom_2_data_2, rom_2_data}));  // open: sel
  Hex_Digit_Display hex_digit_display_7 (.value(bin2dec_1_bcd_output_3));  // open: dp
  Hex_Digit_Display hex_digit_display_8 (.value(bin2dec_1_bcd_output_2));  // open: dp
  assign {or_7_out[15:8], or_7_out_2, or_7_out[3:0]} = and_1_out | and_7_out | and_2_out | and_8_out | or_8_out;  // OR_Gate or_7, 16 bits wide
  assign and_2_out = {16{ALU_Out}} & alu_1_alu_out;  // AND_Gate and_2, 16 bits wide
  Comparator #(.width(16), .mode("unsigned")) comparator_1 (
    .a(A_q), .b(B_q), .gt(comparator_1_gt), .eq(comparator_1_eq), .lt(comparator_1_lt));
  Comparator #(.width(16)) comparator_2 (.a(A_q), .b(B_q), .gt(comparator_2_gt), .lt(comparator_2_lt));  // open: eq
  not not_1 (not_1_out, comparator_2_lt);
  Button button_1 (.out(button_1_out));
  Button button_2 (.out(button_2_out));
  Button button_3 (.out(button_3_out));
  Button button_4 (.out(button_4_out));
  Hex_Digit_Display hex_digit_display_9 (.value(bin2dec_1_bcd_output));  // open: dp
  assign or_8_out = and_3_out | and_4_out | or_29_out | and_5_out | and_6_out;  // OR_Gate or_8, 16 bits wide
  not not_2 (not_2_out, comparator_1_gt);
  not not_3 (not_3_out, comparator_1_eq);
  not not_4 (not_4_out, comparator_1_lt);
  not not_5 (not_5_out, comparator_2_gt);
  Decoder #(.select(4), .disabled(0), .enable("false")) decoder_1 (
    .out1(decoder_1_out1), .out2(decoder_1_out2), .out3(decoder_1_out3), .out4(decoder_1_out4),
    .out5(decoder_1_out5), .out6(decoder_1_out6), .out7(decoder_1_out7), .out8(decoder_1_out8),
    .out9(decoder_1_out9), .out10(decoder_1_out10), .sel(rom_2_data_3));  // open: out0, out11, out12, out13, out14, out15
  or or_9 (ALU_Out, rom_2_data[10], in_8);
  or or_10 (AX_In, rom_2_data[11], button_1_out);
  or or_11 (BX_In, rom_2_data[12], button_2_out);
  or or_12 (CX_In, rom_2_data[13], button_3_out);
  or or_13 (DX_In, rom_2_data[14], button_4_out);
  assign and_3_out = {16{DX_Out}} & DX_q;  // AND_Gate and_3, 16 bits wide
  Bin2Dec bin2dec_1 (
    .BCD_Output({bin2dec_1_bcd_output_5, bin2dec_1_bcd_output_4, bin2dec_1_bcd_output_3, bin2dec_1_bcd_output_2, bin2dec_1_bcd_output}),
    .Negative(bin2dec_1_negative), .Input_Number({or_7_out[15:8], or_7_out_2, or_7_out[3:0]}), .Signed(Signed));  // open: out_5
  assign and_4_out = {16{CX_Out}} & CX_q;  // AND_Gate and_4, 16 bits wide
  assign and_5_out = {16{BX_Out}} & BX_q;  // AND_Gate and_5, 16 bits wide
  assign and_6_out = {16{AX_Out}} & AX_q;  // AND_Gate and_6, 16 bits wide
  assign and_7_out = {16{PC_Out}} & out_19;  // AND_Gate and_7, 16 bits wide
  Register #(.width(16), .trigger("falling")) MAR (
    .D({or_7_out[15:8], or_7_out_2, or_7_out[3:0]}), .Q(MAR_q), .clk(MAR_In));  // open: en, clr
  Register #(.width(16), .trigger("falling")) AX (
    .D({or_7_out[15:8], or_7_out_2, or_7_out[3:0]}), .Q(AX_q), .clk(AX_In));  // open: en, clr
  PC pc_1 (.Set(PC_Set), .PC_Data({or_7_out[15:8], or_7_out_2, or_7_out[3:0]}), .Increment(PC_Inc), .PC_Out(out_19));
  Button button_5 (.out(button_5_out));
  Button button_6 (.out(button_6_out));
  Button button_7 (.out(button_7_out));
  Button button_8 (.out(button_8_out));
  Button button_9 (.out(button_9_out));
  Button button_10 (.out(button_10_out));
  Register #(.width(16), .trigger("falling")) BX (
    .D({or_7_out[15:8], or_7_out_2, or_7_out[3:0]}), .Q(BX_q), .clk(BX_In));  // open: en, clr
  assign and_8_out = {16{RAM_Out}} & ram_1_data;  // AND_Gate and_8, 16 bits wide
  RAM #(.addrWidth(16), .dataWidth(16), .bus("separate")) ram_1 (
    .addr(MAR_q), .din({or_7_out[15:8], or_7_out_2, or_7_out[3:0]}), .data(ram_1_data), .clk(not_6_out));  // open: str, sel, ld, clr
  not not_6 (not_6_out, RAM_In);
  and JA (JA_out, comparator_1_gt, decoder_1_out1);
  and JNA (JNA_out, not_2_out, decoder_1_out2);
  and JE (JE_out, comparator_1_eq, decoder_1_out3);
  and JNE (JNE_out, not_3_out, decoder_1_out4);
  and JB (JB_out, comparator_1_lt, decoder_1_out5);
  and JNB (JNB_out, not_4_out, decoder_1_out6);
  and JG (JG_out, comparator_2_gt, decoder_1_out7);
  and JNG (JNG_out, not_5_out, decoder_1_out8);
  and JL (JL_out, comparator_2_lt, decoder_1_out9);
  and JNL (JNL_out, not_1_out, decoder_1_out10);
  or or_14 (PC_Set, rom_2_data[5], or_23_out, in_9);
  or or_15 (RAM_In, rom_2_data[6], button_5_out);
  or or_16 (Reset_Counter, rom_2_data[7], button_6_out);
  or or_17 (A_In, rom_2_data[8], button_7_out);
  or or_18 (B_In, rom_2_data[9], button_8_out);
  or or_19 (BP_Out, rom_2_data_2[0], in_16);
  or or_20 (BP_In, rom_2_data_2[1], button_9_out);
  or or_21 (SP_Out, rom_2_data_2[2], in_17);
  or or_22 (SP_In, rom_2_data_2[3], button_10_out);
  Register #(.width(16), .trigger("falling")) DX (
    .D({or_7_out[15:8], or_7_out_2, or_7_out[3:0]}), .Q(DX_q), .clk(DX_In));  // open: en, clr
  Register #(.width(16), .trigger("falling")) CX (
    .D({or_7_out[15:8], or_7_out_2, or_7_out[3:0]}), .Q(CX_q), .clk(CX_In));  // open: en, clr
  or or_23 (or_23_out, JA_out, JNA_out, JE_out, JNE_out, JB_out, JNB_out, JG_out, JNG_out, JL_out, JNL_out);
  Register #(.width(16), .trigger("falling")) BP (
    .D({or_7_out[15:8], or_7_out_2, or_7_out[3:0]}), .Q(BP_q), .clk(BP_In));  // open: en, clr
  Register #(.width(16), .trigger("falling")) SP (
    .D({or_7_out[15:8], or_7_out_2, or_7_out[3:0]}), .Q(SP_q), .clk(SP_In));  // open: en, clr
  Button button_11 (.out(button_11_out));
  Button button_12 (.out(button_12_out));
  Button button_13 (.out(button_13_out));
  assign and_9_out = BP_q & {16{BP_Out}};  // AND_Gate and_9, 16 bits wide
  assign and_10_out = SP_q & {16{SP_Out}};  // AND_Gate and_10, 16 bits wide
  or or_24 (PC_Out, rom_2_data[0], rom_1_data_2[0], in_10);
  or or_25 (MAR_In, rom_2_data[1], rom_1_data_2[1], button_11_out);
  or or_26 (RAM_Out, rom_2_data[2], rom_1_data_2[2], in_13);
  or or_27 (I_In, rom_2_data[3], rom_1_data_2[3], button_12_out);
  or or_28 (PC_Inc, rom_2_data[4], rom_1_data_2[3], button_13_out);
  assign or_29_out = and_9_out | and_10_out;  // OR_Gate or_29, 16 bits wide

  // Other names for the same wires on the sheet: Operation_Select[3:0] = out_18

  // Notes on the sheet:
  //   Micro Instructions
  //   Micro Controller
  //   contents of rom_1 (hex, n*v repeats v):
  //   0 3 c 0 10 20 30 40 50 60 70 80 90 a0 b0 c0 d0 e0 f0
  //   contents of rom_2 (hex, n*v repeats v):
  //   0 80 255*0 3 814 80 13*0 3 1014 80 13*0 3 2014 80 13*0 3 4014 80 13*0 3 200014 80 13*0 3 800014 80
  //   173*0 3 0 16 804 80 11*0 3 0 16 1004 80 11*0 3 0 16 2004 80 11*0 3 0 16 4004 80 11*0 3 0 16 200004
  //   80 11*0 3 0 16 800004 80 171*0 3 0 16 8040 80 11*0 3 0 16 10040 80 11*0 3 0 16 20040 80 11*0 3 0 16
  //   40040 80 11*0 3 0 16 100040 80 11*0 3 0 16 400040 80 171*0 3 8100 214 c00 80 11*0 3 10100 214 1400
  //   80 11*0 3 20100 214 2400 80 11*0 3 40100 214 4400 80 11*0 3 100100 214 200400 80 11*0 3 400100 214
  //   800400 80 11*0 3 214 3 10 6 104 440 80 152*0 3 8100 6 214 c00 80 10*0 3 10100 6 214 1400 80 10*0 3
  //   20100 6 214 2400 80 10*0 3 40100 6 214 4400 80 10*0 3 100100 6 214 200400 80 10*0 3 400100 6 214
  //   800400 80 170*0 3 8200 6 114 440 80 10*0 3 10200 6 114 440 80 10*0 3 20200 6 114 440 80 10*0 3 40200
  //   6 114 440 80 10*0 3 100200 6 114 440 80 10*0 3 400200 6 114 440 80 170*0 3 8100 214 1000c00 80 11*0
  //   3 10100 214 1001400 80 11*0 3 20100 214 1002400 80 11*0 3 40100 214 1004400 80 11*0 3 100100 214
  //   1200400 80 11*0 3 400100 214 1800400 80 11*0 3 214 3 10 6 104 1000440 80 152*0 3 8100 6 214 1000c00
  //   80 10*0 3 10100 6 214 1001400 80 10*0 3 20100 6 214 1002400 80 10*0 3 40100 6 214 1004400 80 10*0 3
  //   100100 6 214 1200400 80 10*0 3 400100 6 214 1800400 80 170*0 3 8200 6 114 1000440 80 10*0 3 10200 6
  //   114 1000440 80 10*0 3 20200 6 114 1000440 80 10*0 3 40200 6 114 1000440 80 10*0 3 100200 6 114
  //   1000440 80 10*0 3 400200 6 114 1000440 80 170*0 3 8100 214 2000c00 80 11*0 3 10100 214 2001400 80
  //   11*0 3 20100 214 2002400 80 11*0 3 40100 214 2004400 80 11*0 3 100100 214 2200400 80 11*0 3 400100
  //   214 2800400 80 11*0 3 214 3 10 6 104 2000440 80 152*0 3 8100 6 214 2000c00 80 10*0 3 10100 6 214
  //   2001400 80 10*0 3 20100 6 214 2002400 80 10*0 3 40100 6 214 2004400 80 10*0 3 100100 6 214 2200400
  //   80 10*0 3 400100 6 214 2800400 80 170*0 3 8200 6 114 2000440 80 10*0 3 10200 6 114 2000440 80 10*0 3
  //   20200 6 114 2000440 80 10*0 3 40200 6 114 2000440 80 10*0 3 100200 6 114 2000440 80 10*0 3 400200 6
  //   114 2000440 80 170*0 3 8100 214 3000c00 80 11*0 3 10100 214 3001400 80 11*0 3 20100 214 3002400 80
  //   11*0 3 40100 214 3004400 80 11*0 3 100100 214 3200400 80 11*0 3 400100 214 3800400 80 11*0 3 214 3
  //   10 6 104 3000440 80 152*0 3 8100 6 214 3000c00 80 10*0 3 10100 6 214 3001400 80 10*0 3 20100 6 214
  //   3002400 80 10*0 3 40100 6 214 3004400 80 10*0 3 100100 6 214 3200400 80 10*0 3 400100 6 214 3800400
  //   80 170*0 3 8200 6 114 3000440 80 10*0 3 10200 6 114 3000440 80 10*0 3 20200 6 114 3000440 80 10*0 3
  //   40200 6 114 3000440 80 10*0 3 100200 6 114 3000440 80 10*0 3 400200 6 114 3000440 80 170*0 8800 80
  //   14*0 10800 80 14*0 20800 80 14*0 40800 80 14*0 100800 80 14*0 400800 80 174*0 9000 80 14*0 11000 80
  //   14*0 21000 80 14*0 41000 80 14*0 101000 80 14*0 401000 80 174*0 a000 80 14*0 12000 80 14*0 22000 80
  //   14*0 42000 80 14*0 102000 80 14*0 402000 80 174*0 c000 80 14*0 14000 80 14*0 24000 80 14*0 44000 80
  //   14*0 104000 80 14*0 404000 80 174*0 208000 80 14*0 210000 80 14*0 220000 80 14*0 240000 80 14*0
  //   300000 80 14*0 600000 80 174*0 808000 80 14*0 810000 80 14*0 820000 80 14*0 840000 80 14*0 900000 80
  //   14*0 c00000 80 2734*0 8002 804 80 13*0 10002 804 80 13*0 20002 804 80 13*0 40002 804 80 13*0 100002
  //   804 80 13*0 400002 804 80 173*0 8002 1004 80 13*0 10002 1004 80 13*0 20002 1004 80 13*0 40002 1004
  //   80 13*0 100002 1004 80 13*0 400002 1004 80 173*0 8002 2004 80 13*0 10002 2004 80 13*0 20002 2004 80
  //   13*0 40002 2004 80 13*0 100002 2004 80 13*0 400002 2004 80 173*0 8002 4004 80 13*0 10002 4004 80
  //   13*0 20002 4004 80 13*0 40002 4004 80 13*0 100002 4004 80 13*0 400002 4004 80 173*0 8002 200004 80
  //   13*0 10002 200004 80 13*0 20002 200004 80 13*0 40002 200004 80 13*0 100002 200004 80 13*0 400002
  //   200004 80 173*0 8002 800004 80 13*0 10002 800004 80 13*0 20002 800004 80 13*0 40002 800004 80 13*0
  //   100002 800004 80 13*0 400002 800004 80 2733*0 8002 8040 80 13*0 8002 10040 80 29*0 8002 40040 80
  //   13*0 8002 100040 80 13*0 8002 400040 80 173*0 10002 8040 80 13*0 10002 10040 80 29*0 10002 40040 80
  //   13*0 10002 100040 80 13*0 10002 400040 8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
  //   RAM
endmodule

module Clock (
  input  Power,
  input  Manual_Override,
  input  Manual_Tick,
  input  Halt,
  output Out
);

  wire and_1_out, and_2_out, clock_1_out, not_1_out, not_2_out, or_1_out;

  Clock_part clock_1 (.out(clock_1_out));
  not not_1 (not_1_out, Manual_Override);
  and and_1 (and_1_out, not_1_out, clock_1_out);
  and and_2 (and_2_out, Manual_Override, Manual_Tick);
  or or_1 (or_1_out, and_1_out, and_2_out);
  not not_2 (not_2_out, Halt);
  and and_3 (Out, Power, not_2_out, or_1_out);
endmodule

module ALU (
  input  [3:0] Operation,
  input  [15:0] A,
  input  [15:0] B,
  output [15:0] ALU_Out
);

  wire [15:0] adder_1_out, adder_2_out, and_1_out, divider_1_out, multiplier_1_out, negator_1_out, not_1_out,
       or_1_out, shifter_1_out, shifter_2_out, shifter_3_out, shifter_4_out, shifter_5_out, subtractor_1_out,
       subtractor_2_out, xor_1_out;

  Adder #(.width(16)) adder_1 (.a(A), .b(B), .out(adder_1_out));  // open: cin, cout
  Subtractor #(.width(16)) subtractor_1 (.a(A), .b(B), .out(subtractor_1_out));  // open: bin, bout
  Multiplier #(.width(16)) multiplier_1 (.a(A), .b(B), .out(multiplier_1_out));  // open: cin, cout
  Divider #(.width(16)) divider_1 (.a(A), .b(B), .out(divider_1_out));  // open: upper, rem
  Shifter #(.width(16)) shifter_1 (.in(A), .\dist (B[3:0]), .out(shifter_1_out));
  Shifter #(.width(16), .shift("lr")) shifter_2 (.in(A), .\dist (B[3:0]), .out(shifter_2_out));
  Shifter #(.width(16), .shift("ar")) shifter_3 (.in(A), .\dist (B[3:0]), .out(shifter_3_out));
  Shifter #(.width(16), .shift("rl")) shifter_4 (.in(A), .\dist (B[3:0]), .out(shifter_4_out));
  Shifter #(.width(16), .shift("rr")) shifter_5 (.in(A), .\dist (B[3:0]), .out(shifter_5_out));
  assign and_1_out = A & B;  // AND_Gate and_1, 16 bits wide
  assign or_1_out = A | B;  // OR_Gate or_1, 16 bits wide
  assign xor_1_out = A ^ B;  // XOR_Gate xor_1, 16 bits wide
  assign not_1_out = ~A;  // NOT_Gate not_1, 16 bits wide
  Negator #(.width(16)) negator_1 (.in(A), .out(negator_1_out));
  Adder #(.width(16)) adder_2 (.a(A), .b(16'h1), .out(adder_2_out));  // open: cin, cout
  Subtractor #(.width(16)) subtractor_2 (.a(A), .b(16'h1), .out(subtractor_2_out));  // open: bin, bout
  Multiplexer #(.select(4), .width(16), .disabled(0), .enable("false")) multiplexer_1 (
    .in0(adder_1_out), .in1(subtractor_1_out), .in2(multiplier_1_out), .in3(divider_1_out),
    .in4(shifter_1_out), .in5(shifter_2_out), .in6(shifter_3_out), .in7(shifter_4_out), .in8(shifter_5_out),
    .in9(and_1_out), .in10(or_1_out), .in11(xor_1_out), .in12(not_1_out), .in13(negator_1_out),
    .in14(adder_2_out), .in15(subtractor_2_out), .out(ALU_Out), .sel(Operation));
endmodule

module PC (
  input  Set,
  input  [15:0] PC_Data,
  input  Increment,
  output [15:0] PC_Out
);

  wire and_1_out, buffer_1_out, buffer_2_out, buffer_3_out, buffer_4_out, buffer_5_out, buffer_6_out,
       buffer_7_out, not_1_out, not_2_out, or_1_out;
  wire [15:0] adder_1_out, multiplexer_1_out;

  buf buffer_1 (buffer_1_out, buffer_2_out);
  buf buffer_2 (buffer_2_out, buffer_3_out);
  buf buffer_3 (buffer_3_out, Set);
  buf buffer_4 (buffer_4_out, buffer_1_out);
  Adder #(.width(16)) adder_1 (.a(PC_Out), .b(16'h1), .out(adder_1_out));  // open: cin, cout
  buf buffer_5 (buffer_5_out, buffer_4_out);
  buf buffer_6 (buffer_6_out, buffer_5_out);
  buf buffer_7 (buffer_7_out, buffer_6_out);
  Multiplexer #(.width(16), .disabled(0), .enable("false")) multiplexer_1 (
    .in0(adder_1_out), .in1(PC_Data), .out(multiplexer_1_out), .sel(buffer_7_out));
  and and_1 (and_1_out, not_1_out, not_2_out);
  or or_1 (or_1_out, Set, Increment);
  not not_1 (not_1_out, or_1_out);
  not not_2 (not_2_out, not_1_out);
  Register #(.width(16)) register_1 (.D(multiplexer_1_out), .Q(PC_Out), .clk(and_1_out));  // open: en, clr
endmodule

// B2D
module Bin2Dec (
  input  Signed,
  input  [15:0] Input_Number,
  output [19:0] BCD_Output,
  output Negative,
  output [15:0] out_5
);

  wire bin2dec_add3_1_out_6, bin2dec_add3_1_out_7, bin2dec_add3_1_out_8, bin2dec_add3_2_out_6,
       bin2dec_add3_2_out_7, bin2dec_add3_2_out_8, bin2dec_add3_3_out_5, bin2dec_add3_3_out_6,
       bin2dec_add3_3_out_7, bin2dec_add3_3_out_8, bin2dec_add3_4_out_5, bin2dec_add3_4_out_6,
       bin2dec_add3_4_out_7, bin2dec_add3_4_out_8, bin2dec_add3_5_out_5, bin2dec_add3_5_out_6,
       bin2dec_add3_5_out_7, bin2dec_add3_5_out_8, bin2dec_add3_8_out_5, bin2dec_add3_8_out_6,
       bin2dec_add3_8_out_7, bin2dec_add3_8_out_8, bin2dec_add3_9_out_5, bin2dec_add3_9_out_6,
       bin2dec_add3_9_out_7, bin2dec_add3_9_out_8, bin2dec_add3_10_out_5, bin2dec_add3_10_out_6,
       bin2dec_add3_10_out_7, bin2dec_add3_10_out_8, bin2dec_add3_11_out_5, bin2dec_add3_11_out_6,
       bin2dec_add3_11_out_7, bin2dec_add3_11_out_8, bin2dec_add3_12_out_5, bin2dec_add3_12_out_6,
       bin2dec_add3_12_out_7, bin2dec_add3_12_out_8, bin2dec_add3_13_out_5, bin2dec_add3_13_out_6,
       bin2dec_add3_13_out_7, bin2dec_add3_13_out_8, bin2dec_add3_14_out_5, bin2dec_add3_14_out_6,
       bin2dec_add3_14_out_7, bin2dec_add3_14_out_8, bin2dec_add3_15_out_5, bin2dec_add3_15_out_6,
       bin2dec_add3_15_out_7, bin2dec_add3_15_out_8, bin2dec_add3_16_out_5, bin2dec_add3_16_out_6,
       bin2dec_add3_16_out_7, bin2dec_add3_16_out_8, bin2dec_add3_17_out_5, bin2dec_add3_17_out_6,
       bin2dec_add3_17_out_7, bin2dec_add3_17_out_8, bin2dec_add3_18_out_5, bin2dec_add3_18_out_6,
       bin2dec_add3_18_out_7, bin2dec_add3_18_out_8, bin2dec_add3_19_out_5, bin2dec_add3_19_out_6,
       bin2dec_add3_19_out_7, bin2dec_add3_19_out_8, bin2dec_add3_20_out_5, bin2dec_add3_20_out_6,
       bin2dec_add3_20_out_7, bin2dec_add3_20_out_8, bin2dec_add3_21_out_5, bin2dec_add3_21_out_6,
       bin2dec_add3_21_out_7, bin2dec_add3_21_out_8, bin2dec_add3_22_out_5, bin2dec_add3_22_out_6,
       bin2dec_add3_22_out_7, bin2dec_add3_22_out_8, bin2dec_add3_23_out_5, bin2dec_add3_23_out_6,
       bin2dec_add3_23_out_7, bin2dec_add3_23_out_8, bin2dec_add3_24_out_5, bin2dec_add3_24_out_6,
       bin2dec_add3_24_out_7, bin2dec_add3_24_out_8, bin2dec_add3_25_out_5, bin2dec_add3_25_out_6,
       bin2dec_add3_25_out_7, bin2dec_add3_25_out_8, bin2dec_add3_26_out_5, bin2dec_add3_26_out_6,
       bin2dec_add3_26_out_7, bin2dec_add3_26_out_8, bin2dec_add3_27_out_5, bin2dec_add3_27_out_6,
       bin2dec_add3_27_out_7, bin2dec_add3_27_out_8, bin2dec_add3_30_out_5, bin2dec_add3_30_out_6,
       bin2dec_add3_30_out_7, bin2dec_add3_30_out_8, bin2dec_add3_31_out_5, bin2dec_add3_31_out_6,
       bin2dec_add3_31_out_7, bin2dec_add3_31_out_8, bin2dec_add3_32_out_5, bin2dec_add3_32_out_6,
       bin2dec_add3_32_out_7, bin2dec_add3_32_out_8, bin2dec_add3_33_out_5, bin2dec_add3_33_out_6,
       bin2dec_add3_33_out_7, bin2dec_add3_33_out_8;
  wire [15:1] multiplexer_1_out;

  and and_1 (Negative, Input_Number[15], Signed);
  Hex_Digit_Display hex_digit_display_1 (.value(BCD_Output[15:12]));  // open: dp
  Hex_Digit_Display hex_digit_display_2 (.value({1'b0, BCD_Output[18:16]}));  // open: dp
  Hex_Digit_Display hex_digit_display_3 (.value(BCD_Output[7:4]));  // open: dp
  Hex_Digit_Display hex_digit_display_4 (.value(BCD_Output[11:8]));  // open: dp
  Negator #(.width(16)) negator_1 (.in(Input_Number), .out(out_5));
  Bin2Dec_add3 bin2dec_add3_1 (
    .out_5(BCD_Output[17]), .out_6(bin2dec_add3_1_out_6), .out_7(bin2dec_add3_1_out_7),
    .out_8(bin2dec_add3_1_out_8), .in_1(bin2dec_add3_2_out_6), .in_2(bin2dec_add3_2_out_7),
    .in_3(bin2dec_add3_2_out_8), .in_4(bin2dec_add3_10_out_5));
  Bin2Dec_add3 bin2dec_add3_2 (
    .out_5(BCD_Output[18]), .out_6(bin2dec_add3_2_out_6), .out_7(bin2dec_add3_2_out_7),
    .out_8(bin2dec_add3_2_out_8), .in_1(bin2dec_add3_4_out_5), .in_2(bin2dec_add3_3_out_5),
    .in_3(bin2dec_add3_15_out_5), .in_4(bin2dec_add3_12_out_5));
  Bin2Dec_add3 bin2dec_add3_3 (
    .out_5(bin2dec_add3_3_out_5), .out_6(bin2dec_add3_3_out_6), .out_7(bin2dec_add3_3_out_7),
    .out_8(bin2dec_add3_3_out_8), .in_1(bin2dec_add3_4_out_6), .in_2(bin2dec_add3_4_out_7),
    .in_3(bin2dec_add3_4_out_8), .in_4(bin2dec_add3_19_out_5));
  Bin2Dec_add3 bin2dec_add3_4 (
    .out_5(bin2dec_add3_4_out_5), .out_6(bin2dec_add3_4_out_6), .out_7(bin2dec_add3_4_out_7),
    .out_8(bin2dec_add3_4_out_8), .in_1(1'b0), .in_2(bin2dec_add3_5_out_5), .in_3(bin2dec_add3_22_out_5),
    .in_4(bin2dec_add3_21_out_5));
  Hex_Digit_Display hex_digit_display_5 (.value(BCD_Output[3:0]));  // open: dp
  Bin2Dec_add3 bin2dec_add3_5 (
    .out_5(bin2dec_add3_5_out_5), .out_6(bin2dec_add3_5_out_6), .out_7(bin2dec_add3_5_out_7),
    .out_8(bin2dec_add3_5_out_8), .in_1(1'b0), .in_2(bin2dec_add3_27_out_5), .in_3(bin2dec_add3_26_out_5),
    .in_4(bin2dec_add3_25_out_5));
  Multiplexer #(.width(16), .enable("false")) multiplexer_1 (
    .in0(Input_Number), .in1(out_5), .out({multiplexer_1_out, BCD_Output[0]}), .sel(Negative));
  Bin2Dec_add3 bin2dec_add3_6 (
    .out_5(BCD_Output[12]), .out_6(BCD_Output[11]), .out_7(BCD_Output[10]), .out_8(BCD_Output[9]),
    .in_1(bin2dec_add3_9_out_6), .in_2(bin2dec_add3_9_out_7), .in_3(bin2dec_add3_9_out_8),
    .in_4(bin2dec_add3_8_out_5));
  Bin2Dec_add3 bin2dec_add3_7 (
    .out_5(BCD_Output[16]), .out_6(BCD_Output[15]), .out_7(BCD_Output[14]), .out_8(BCD_Output[13]),
    .in_1(bin2dec_add3_1_out_6), .in_2(bin2dec_add3_1_out_7), .in_3(bin2dec_add3_1_out_8),
    .in_4(bin2dec_add3_9_out_5));
  Bin2Dec_add3 bin2dec_add3_8 (
    .out_5(bin2dec_add3_8_out_5), .out_6(bin2dec_add3_8_out_6), .out_7(bin2dec_add3_8_out_7),
    .out_8(bin2dec_add3_8_out_8), .in_1(bin2dec_add3_11_out_6), .in_2(bin2dec_add3_11_out_7),
    .in_3(bin2dec_add3_11_out_8), .in_4(bin2dec_add3_31_out_5));
  Bin2Dec_add3 bin2dec_add3_9 (
    .out_5(bin2dec_add3_9_out_5), .out_6(bin2dec_add3_9_out_6), .out_7(bin2dec_add3_9_out_7),
    .out_8(bin2dec_add3_9_out_8), .in_1(bin2dec_add3_10_out_6), .in_2(bin2dec_add3_10_out_7),
    .in_3(bin2dec_add3_10_out_8), .in_4(bin2dec_add3_11_out_5));
  Bin2Dec_add3 bin2dec_add3_10 (
    .out_5(bin2dec_add3_10_out_5), .out_6(bin2dec_add3_10_out_6), .out_7(bin2dec_add3_10_out_7),
    .out_8(bin2dec_add3_10_out_8), .in_1(bin2dec_add3_12_out_6), .in_2(bin2dec_add3_12_out_7),
    .in_3(bin2dec_add3_12_out_8), .in_4(bin2dec_add3_13_out_5));
  Bin2Dec_add3 bin2dec_add3_11 (
    .out_5(bin2dec_add3_11_out_5), .out_6(bin2dec_add3_11_out_6), .out_7(bin2dec_add3_11_out_7),
    .out_8(bin2dec_add3_11_out_8), .in_1(bin2dec_add3_13_out_6), .in_2(bin2dec_add3_13_out_7),
    .in_3(bin2dec_add3_13_out_8), .in_4(bin2dec_add3_32_out_5));
  Bin2Dec_add3 bin2dec_add3_12 (
    .out_5(bin2dec_add3_12_out_5), .out_6(bin2dec_add3_12_out_6), .out_7(bin2dec_add3_12_out_7),
    .out_8(bin2dec_add3_12_out_8), .in_1(bin2dec_add3_15_out_6), .in_2(bin2dec_add3_15_out_7),
    .in_3(bin2dec_add3_15_out_8), .in_4(bin2dec_add3_14_out_5));
  Bin2Dec_add3 bin2dec_add3_13 (
    .out_5(bin2dec_add3_13_out_5), .out_6(bin2dec_add3_13_out_6), .out_7(bin2dec_add3_13_out_7),
    .out_8(bin2dec_add3_13_out_8), .in_1(bin2dec_add3_14_out_6), .in_2(bin2dec_add3_14_out_7),
    .in_3(bin2dec_add3_14_out_8), .in_4(bin2dec_add3_33_out_5));
  Bin2Dec_add3 bin2dec_add3_14 (
    .out_5(bin2dec_add3_14_out_5), .out_6(bin2dec_add3_14_out_6), .out_7(bin2dec_add3_14_out_7),
    .out_8(bin2dec_add3_14_out_8), .in_1(bin2dec_add3_17_out_6), .in_2(bin2dec_add3_17_out_7),
    .in_3(bin2dec_add3_17_out_8), .in_4(bin2dec_add3_16_out_5));
  Bin2Dec_add3 bin2dec_add3_15 (
    .out_5(bin2dec_add3_15_out_5), .out_6(bin2dec_add3_15_out_6), .out_7(bin2dec_add3_15_out_7),
    .out_8(bin2dec_add3_15_out_8), .in_1(bin2dec_add3_3_out_6), .in_2(bin2dec_add3_3_out_7),
    .in_3(bin2dec_add3_3_out_8), .in_4(bin2dec_add3_17_out_5));
  Bin2Dec_add3 bin2dec_add3_16 (
    .out_5(bin2dec_add3_16_out_5), .out_6(bin2dec_add3_16_out_6), .out_7(bin2dec_add3_16_out_7),
    .out_8(bin2dec_add3_16_out_8), .in_1(bin2dec_add3_18_out_6), .in_2(bin2dec_add3_18_out_7),
    .in_3(bin2dec_add3_18_out_8), .in_4(multiplexer_1_out[6]));
  Bin2Dec_add3 bin2dec_add3_17 (
    .out_5(bin2dec_add3_17_out_5), .out_6(bin2dec_add3_17_out_6), .out_7(bin2dec_add3_17_out_7),
    .out_8(bin2dec_add3_17_out_8), .in_1(bin2dec_add3_19_out_6), .in_2(bin2dec_add3_19_out_7),
    .in_3(bin2dec_add3_19_out_8), .in_4(bin2dec_add3_18_out_5));
  Bin2Dec_add3 bin2dec_add3_18 (
    .out_5(bin2dec_add3_18_out_5), .out_6(bin2dec_add3_18_out_6), .out_7(bin2dec_add3_18_out_7),
    .out_8(bin2dec_add3_18_out_8), .in_1(bin2dec_add3_20_out_6), .in_2(bin2dec_add3_20_out_7),
    .in_3(bin2dec_add3_20_out_8), .in_4(multiplexer_1_out[7]));
  Bin2Dec_add3 bin2dec_add3_19 (
    .out_5(bin2dec_add3_19_out_5), .out_6(bin2dec_add3_19_out_6), .out_7(bin2dec_add3_19_out_7),
    .out_8(bin2dec_add3_19_out_8), .in_1(bin2dec_add3_21_out_6), .in_2(bin2dec_add3_21_out_7),
    .in_3(bin2dec_add3_21_out_8), .in_4(bin2dec_add3_20_out_5));
  Bin2Dec_add3 bin2dec_add3_20 (
    .out_5(bin2dec_add3_20_out_5), .out_6(bin2dec_add3_20_out_6), .out_7(bin2dec_add3_20_out_7),
    .out_8(bin2dec_add3_20_out_8), .in_1(bin2dec_add3_23_out_6), .in_2(bin2dec_add3_23_out_7),
    .in_3(bin2dec_add3_23_out_8), .in_4(multiplexer_1_out[8]));
  Bin2Dec_add3 bin2dec_add3_21 (
    .out_5(bin2dec_add3_21_out_5), .out_6(bin2dec_add3_21_out_6), .out_7(bin2dec_add3_21_out_7),
    .out_8(bin2dec_add3_21_out_8), .in_1(bin2dec_add3_22_out_6), .in_2(bin2dec_add3_22_out_7),
    .in_3(bin2dec_add3_22_out_8), .in_4(bin2dec_add3_23_out_5));
  Bin2Dec_add3 bin2dec_add3_22 (
    .out_5(bin2dec_add3_22_out_5), .out_6(bin2dec_add3_22_out_6), .out_7(bin2dec_add3_22_out_7),
    .out_8(bin2dec_add3_22_out_8), .in_1(bin2dec_add3_5_out_6), .in_2(bin2dec_add3_5_out_7),
    .in_3(bin2dec_add3_5_out_8), .in_4(bin2dec_add3_24_out_5));
  Bin2Dec_add3 bin2dec_add3_23 (
    .out_5(bin2dec_add3_23_out_5), .out_6(bin2dec_add3_23_out_6), .out_7(bin2dec_add3_23_out_7),
    .out_8(bin2dec_add3_23_out_8), .in_1(bin2dec_add3_24_out_6), .in_2(bin2dec_add3_24_out_7),
    .in_3(bin2dec_add3_24_out_8), .in_4(multiplexer_1_out[9]));
  Bin2Dec_add3 bin2dec_add3_24 (
    .out_5(bin2dec_add3_24_out_5), .out_6(bin2dec_add3_24_out_6), .out_7(bin2dec_add3_24_out_7),
    .out_8(bin2dec_add3_24_out_8), .in_1(bin2dec_add3_25_out_6), .in_2(bin2dec_add3_25_out_7),
    .in_3(bin2dec_add3_25_out_8), .in_4(multiplexer_1_out[10]));
  Bin2Dec_add3 bin2dec_add3_25 (
    .out_5(bin2dec_add3_25_out_5), .out_6(bin2dec_add3_25_out_6), .out_7(bin2dec_add3_25_out_7),
    .out_8(bin2dec_add3_25_out_8), .in_1(bin2dec_add3_26_out_6), .in_2(bin2dec_add3_26_out_7),
    .in_3(bin2dec_add3_26_out_8), .in_4(multiplexer_1_out[11]));
  Bin2Dec_add3 bin2dec_add3_26 (
    .out_5(bin2dec_add3_26_out_5), .out_6(bin2dec_add3_26_out_6), .out_7(bin2dec_add3_26_out_7),
    .out_8(bin2dec_add3_26_out_8), .in_1(bin2dec_add3_27_out_6), .in_2(bin2dec_add3_27_out_7),
    .in_3(bin2dec_add3_27_out_8), .in_4(multiplexer_1_out[12]));
  Bin2Dec_add3 bin2dec_add3_27 (
    .out_5(bin2dec_add3_27_out_5), .out_6(bin2dec_add3_27_out_6), .out_7(bin2dec_add3_27_out_7),
    .out_8(bin2dec_add3_27_out_8), .in_1(1'b0), .in_2(multiplexer_1_out[15]), .in_3(multiplexer_1_out[14]),
    .in_4(multiplexer_1_out[13]));
  Bin2Dec_add3 bin2dec_add3_28 (
    .out_5(BCD_Output[8]), .out_6(BCD_Output[7]), .out_7(BCD_Output[6]), .out_8(BCD_Output[5]),
    .in_1(bin2dec_add3_8_out_6), .in_2(bin2dec_add3_8_out_7), .in_3(bin2dec_add3_8_out_8),
    .in_4(bin2dec_add3_30_out_5));
  Bin2Dec_add3 bin2dec_add3_29 (
    .out_5(BCD_Output[4]), .out_6(BCD_Output[3]), .out_7(BCD_Output[2]), .out_8(BCD_Output[1]),
    .in_1(bin2dec_add3_30_out_6), .in_2(bin2dec_add3_30_out_7), .in_3(bin2dec_add3_30_out_8),
    .in_4(multiplexer_1_out[1]));
  Bin2Dec_add3 bin2dec_add3_30 (
    .out_5(bin2dec_add3_30_out_5), .out_6(bin2dec_add3_30_out_6), .out_7(bin2dec_add3_30_out_7),
    .out_8(bin2dec_add3_30_out_8), .in_1(bin2dec_add3_31_out_6), .in_2(bin2dec_add3_31_out_7),
    .in_3(bin2dec_add3_31_out_8), .in_4(multiplexer_1_out[2]));
  Bin2Dec_add3 bin2dec_add3_31 (
    .out_5(bin2dec_add3_31_out_5), .out_6(bin2dec_add3_31_out_6), .out_7(bin2dec_add3_31_out_7),
    .out_8(bin2dec_add3_31_out_8), .in_1(bin2dec_add3_32_out_6), .in_2(bin2dec_add3_32_out_7),
    .in_3(bin2dec_add3_32_out_8), .in_4(multiplexer_1_out[3]));
  Bin2Dec_add3 bin2dec_add3_32 (
    .out_5(bin2dec_add3_32_out_5), .out_6(bin2dec_add3_32_out_6), .out_7(bin2dec_add3_32_out_7),
    .out_8(bin2dec_add3_32_out_8), .in_1(bin2dec_add3_33_out_6), .in_2(bin2dec_add3_33_out_7),
    .in_3(bin2dec_add3_33_out_8), .in_4(multiplexer_1_out[4]));
  Bin2Dec_add3 bin2dec_add3_33 (
    .out_5(bin2dec_add3_33_out_5), .out_6(bin2dec_add3_33_out_6), .out_7(bin2dec_add3_33_out_7),
    .out_8(bin2dec_add3_33_out_8), .in_1(bin2dec_add3_16_out_6), .in_2(bin2dec_add3_16_out_7),
    .in_3(bin2dec_add3_16_out_8), .in_4(multiplexer_1_out[5]));

  assign BCD_Output[19] = 1'b0;
endmodule

// Add3
module Bin2Dec_add3 (
  input  in_1,
  input  in_2,
  input  in_3,
  input  in_4,
  output out_5,
  output out_6,
  output out_7,
  output out_8
);

  wire and_1_out, and_2_out, and_3_out, and_4_out, and_5_out, and_6_out, and_7_out, and_8_out, and_9_out,
       and_10_out, and_11_out, and_12_out, and_13_out, and_14_out, and_15_out, not_1_out, not_2_out,
       not_3_out, not_4_out;

  not not_1 (not_1_out, in_3);
  not not_2 (not_2_out, in_2);
  not not_3 (not_3_out, in_1);
  and and_1 (and_1_out, not_3_out, in_2, not_1_out, in_4);
  not not_4 (not_4_out, in_4);
  or or_1 (out_5, and_1_out, and_2_out, and_3_out, and_4_out, and_5_out);
  and and_2 (and_2_out, not_3_out, in_2, in_3, not_4_out);
  and and_3 (and_3_out, not_3_out, in_2, in_3, in_4);
  and and_4 (and_4_out, in_1, not_2_out, not_1_out, not_4_out);
  and and_5 (and_5_out, in_1, not_2_out, not_1_out, in_4);
  or or_2 (out_6, and_7_out, and_6_out);
  and and_6 (and_6_out, in_1, not_2_out, not_1_out, in_4);
  and and_7 (and_7_out, not_3_out, in_2, not_1_out, not_4_out);
  and and_8 (and_8_out, not_3_out, not_2_out, in_3, not_4_out);
  or or_3 (out_7, and_8_out, and_9_out, and_10_out, and_11_out);
  and and_9 (and_9_out, not_3_out, not_2_out, in_3, in_4);
  and and_10 (and_10_out, not_3_out, in_2, in_3, in_4);
  and and_11 (and_11_out, in_1, not_2_out, not_1_out, not_4_out);
  and and_12 (and_12_out, not_3_out, not_2_out, not_1_out, in_4);
  or or_4 (out_8, and_12_out, and_13_out, and_15_out, and_14_out);
  and and_13 (and_13_out, not_3_out, not_2_out, in_3, in_4);
  and and_14 (and_14_out, in_1, not_2_out, not_1_out, not_4_out);
  and and_15 (and_15_out, not_3_out, in_2, in_3, not_4_out);
endmodule
